// Logisim project Multicycle.circ as structural Verilog: 13 circuits, main circuit main
module main (
);

  wire ALUOp0, ALUOp1, ALUSrcA, ALUSrcB0, ALUSrcB1, and_1_out, clk, IorD, IRWrite, MemRead, MemtoReg,
       MemWrite, PCSource0, PCSource1, PCWE, PCWrite, PCWriteCond, RegDst, RegWrite, Reset, Zero;
  wire [3:0] alu_control_1_op0, control_unit_1_currentstate;
  wire [4:0] multiplexer_4_out, rs, rt;
  wire [5:0] Op;
  wire [15:0] Bit15_0;
  wire [27:0] bit_extender_1_out, PC;
  wire [31:0] A, ALUOut, ALURes, B, bit_extender_2_out, Jump, MDR, multiplexer_1_out, multiplexer_2_out,
       multiplexer_3_out, multiplexer_5_out, multiplexer_6_out, ram_1_dout, shifter_2_out;

  Clock clock_1 (.out(clk));
  Button button_1 (.out(Reset));
  Multiplexer #(.select(2), .width(32)) multiplexer_1 (
    .in0(ALURes), .in1(ALUOut), .in2(Jump), .out(multiplexer_1_out), .sel({PCSource1, PCSource0}));  // open: in3
  Register #(.width(32)) u_PC (.D(multiplexer_1_out), .en(PCWE), .clk(clk), .Q({Jump[31:28], PC}), .clr(Reset));
  Multiplexer #(.width(32)) multiplexer_2 (.in0({Jump[31:28], PC}), .in1(ALUOut), .out(multiplexer_2_out), .sel(IorD));
  and and_1 (and_1_out, PCWriteCond, Zero);
  RAM #(.addrWidth(16), .dataWidth(32)) ram_1 (
    .addr(multiplexer_2_out[15:0]), .we(MemWrite), .oe(MemRead), .clk(clk), .din(B), .dout(ram_1_dout));
  or or_1 (PCWE, and_1_out, PCWrite);
  assign bit_extender_1_out = {{2{rs[4]}}, {rs, rt, Bit15_0}};  // Bit_Extender bit_extender_1
  Shifter #(.width(28)) shifter_1 (.in(bit_extender_1_out), .\dist (5'b00010), .out(Jump[27:0]));
  assign bit_extender_2_out = {{16{Bit15_0[15]}}, Bit15_0};  // Bit_Extender bit_extender_2
  Shifter #(.width(32)) shifter_2 (.in(bit_extender_2_out), .\dist (5'b00010), .out(shifter_2_out));
  Register #(.width(32)) u_MDR (.D(ram_1_dout), .clk(clk), .Q(MDR), .clr(Reset));  // open: en
  InstructionReg instructionreg_1 (
    .in_1(ram_1_dout), .WE(IRWrite), .Clock(clk), .Reset(Reset), .out_5(Bit15_0), .rt(rt), .rs(rs),
    .Opcode(Op));
  ALU_Control alu_control_1 (
    .ALUOp0(ALUOp0), .ALUOp1(ALUOp1), .F3(Bit15_0[3]), .F2(Bit15_0[2]), .F1(Bit15_0[1]), .F0(Bit15_0[0]),
    .Op3(alu_control_1_op0[3]), .Op2(alu_control_1_op0[2]), .Op1(alu_control_1_op0[1]),
    .Op0(alu_control_1_op0[0]));
  Multiplexer #(.select(2), .width(32)) multiplexer_3 (
    .in0(B), .in1(32'h1), .in2(bit_extender_2_out), .in3(shifter_2_out), .out(multiplexer_3_out),
    .sel({ALUSrcB1, ALUSrcB0}));
  Multiplexer #(.width(5)) multiplexer_4 (.in0(rt), .in1(Bit15_0[15:11]), .out(multiplexer_4_out), .sel(RegDst));
  Multiplexer #(.width(32)) multiplexer_5 (.in0(ALUOut), .in1(MDR), .out(multiplexer_5_out), .sel(MemtoReg));
  Multiplexer #(.width(32)) multiplexer_6 (.in0({Jump[31:28], PC}), .in1(A), .out(multiplexer_6_out), .sel(ALUSrcA));
  Control_unit control_unit_1 (
    .Opcode(Op), .Clock(clk), .Reset(Reset), .PCWrite(PCWrite), .PCWriteCond(PCWriteCond), .IorD(IorD),
    .MemRead(MemRead), .MemWrite(MemWrite), .IRWrite(IRWrite), .MemroReg(MemtoReg), .PCSource1(PCSource1),
    .PCSource0(PCSource0), .ALUOp1(ALUOp1), .ALUOp0(ALUOp0), .ALUSrcB1(ALUSrcB1), .ALUSrcB0(ALUSrcB0),
    .ALUSrcA(ALUSrcA), .RegWrite(RegWrite), .RegDst(RegDst), .CurrentState(control_unit_1_currentstate));
  // Probe on control_unit_1_currentstate
  RegFile regfile_1 (
    .rs(rs), .rt(rt), .WrAddr(multiplexer_4_out), .WriteData(multiplexer_5_out), .WrReg(RegWrite),
    .in_6(clk), .Reset(Reset), .RdData1(A), .RdData2(B));
  ALU alu_1 (
    .Op(alu_control_1_op0), .A(multiplexer_6_out), .B(multiplexer_3_out), .Shamt(Bit15_0[10:6]),
    .Res(ALURes), .Zero(Zero));
  Register #(.width(32)) u_ALUOut (.D(ALURes), .clk(clk), .Q(ALUOut), .clr(Reset));  // open: en

  // Other names for the same wires on the sheet: PC[31:28] = Jump[31:28]
endmodule

module Datapath_outputs (
  input  [3:0] S,
  output PCWrite,
  output PCWriteCond,
  output IorD,
  output MemRead,
  output MemWrite,
  output IRWrite,
  output MemtoReg,
  output PCSource1,
  output PCSource0,
  output ALUOp1,
  output ALUOp0,
  output ALUSrcB1,
  output ALUSrcB0,
  output ALUSrcA,
  output RegWrite,
  output RegDst
);

  wire nand_1_out, nand_2_out, nand_3_out, nand_4_out, nand_5_out, nand_6_out, nand_7_out, nand_8_out,
       nand_9_out, nand_10_out, nand_11_out, nand_12_out, nand_13_out, nand_14_out, nand_15_out, nand_16_out,
       nand_17_out, nand_18_out, nand_19_out, nand_20_out, nand_21_out, nand_22_out, nand_23_out,
       nand_24_out, nand_25_out, nand_26_out, nand_27_out, nand_28_out, nand_29_out, nand_30_out,
       nand_31_out, nand_32_out, nand_33_out, nand_34_out, nand_35_out, nand_36_out, nand_37_out,
       nand_38_out, nand_39_out, nand_40_out, nand_41_out, nand_42_out, nand_43_out, nand_44_out,
       nand_45_out, nand_46_out, nand_47_out, nand_48_out, nand_49_out, nand_50_out, nand_51_out,
       nand_52_out, nand_53_out, nand_54_out, nand_55_out, nand_56_out, nand_57_out, nand_58_out,
       nand_59_out, nand_60_out, nand_61_out, nand_62_out, nand_63_out, nand_64_out, nand_65_out,
       nand_66_out, nand_67_out, nand_68_out, nand_69_out, nand_70_out, nand_71_out, nand_72_out,
       nand_73_out, nand_75_out, nand_76_out, nand_77_out, nand_78_out, nand_79_out, nand_80_out,
       nand_81_out, nand_82_out, nand_83_out, nand_84_out, nand_85_out, nand_86_out, nand_87_out,
       nand_88_out, nand_89_out, nand_90_out, nand_91_out, nand_92_out, nand_93_out, nand_94_out,
       nand_95_out, nand_96_out, nand_97_out, nand_98_out, nand_99_out, nand_100_out, nand_101_out,
       nand_102_out, nand_103_out, nand_104_out, nand_105_out, nand_106_out, nand_107_out, nand_108_out,
       nand_109_out, nand_111_out, nand_112_out, nand_114_out, nand_115_out, nand_116_out, nand_117_out,
       nand_118_out, nand_119_out, nand_120_out, nand_121_out, nand_123_out, nand_124_out, nand_125_out,
       nand_126_out, nand_127_out, nand_133_out, nand_134_out, nand_135_out, nand_136_out, nand_138_out,
       nand_139_out, nand_140_out, nand_141_out, nand_142_out, nand_143_out;

  nand nand_1 (nand_1_out, 1'b1, S[3]);
  nand nand_2 (nand_2_out, 1'b1, S[2]);
  nand nand_3 (nand_3_out, 1'b1, S[1]);
  nand nand_4 (nand_4_out, 1'b1, S[0]);
  nand nand_5 (nand_5_out, nand_1_out, nand_2_out);
  nand nand_6 (nand_6_out, nand_3_out, nand_4_out);
  nand nand_7 (nand_7_out, S[3], nand_2_out);
  nand nand_8 (nand_8_out, nand_3_out, S[0]);
  nand nand_9 (nand_9_out, S[3], nand_2_out);
  nand nand_10 (nand_10_out, nand_3_out, nand_4_out);
  nand nand_11 (nand_11_out, nand_1_out, nand_2_out);
  nand nand_12 (nand_12_out, S[1], S[0]);
  nand nand_13 (nand_13_out, nand_1_out, S[2]);
  nand nand_14 (nand_14_out, nand_3_out, S[0]);
  nand nand_15 (nand_15_out, nand_1_out, nand_2_out);
  nand nand_16 (nand_16_out, nand_3_out, nand_4_out);
  nand nand_17 (nand_17_out, nand_1_out, nand_2_out);
  nand nand_18 (nand_18_out, S[1], S[0]);
  nand nand_19 (nand_19_out, nand_1_out, S[2]);
  nand nand_20 (nand_20_out, nand_3_out, S[0]);
  nand nand_21 (nand_21_out, 1'b1, S[3]);
  nand nand_22 (nand_22_out, 1'b1, S[2]);
  nand nand_23 (nand_23_out, 1'b1, S[1]);
  nand nand_24 (nand_24_out, 1'b1, S[0]);
  nand nand_25 (nand_25_out, 1'b1, S[3]);
  nand nand_26 (nand_26_out, 1'b1, S[2]);
  nand nand_27 (nand_27_out, 1'b1, S[1]);
  nand nand_28 (nand_28_out, 1'b1, S[0]);
  nand nand_29 (nand_29_out, 1'b1, S[1]);
  nand nand_30 (nand_30_out, 1'b1, S[1]);
  nand nand_31 (nand_31_out, S[3], S[0]);
  nand nand_32 (nand_32_out, S[3], S[0]);
  nand nand_33 (nand_33_out, 1'b1, S[0]);
  nand nand_34 (nand_34_out, 1'b1, S[0]);
  nand nand_35 (nand_35_out, S[2], S[1]);
  nand nand_36 (nand_36_out, S[2], S[1]);
  nand nand_37 (nand_37_out, 1'b1, S[0]);
  nand nand_38 (nand_38_out, 1'b1, S[0]);
  nand nand_39 (nand_39_out, 1'b1, S[3]);
  nand nand_40 (nand_40_out, 1'b1, S[2]);
  nand nand_41 (nand_41_out, 1'b1, S[1]);
  nand nand_42 (nand_42_out, 1'b1, S[2]);
  nand nand_43 (nand_43_out, 1'b1, S[3]);
  nand nand_44 (nand_44_out, 1'b1, S[2]);
  nand nand_45 (nand_45_out, 1'b1, S[3]);
  nand nand_46 (nand_46_out, 1'b1, S[2]);
  nand nand_47 (nand_47_out, 1'b1, S[0]);
  nand nand_48 (nand_48_out, 1'b1, S[0]);
  nand nand_49 (nand_49_out, 1'b1, S[1]);
  nand nand_50 (nand_50_out, S[2], S[1]);
  nand nand_51 (nand_51_out, S[2], S[1]);
  nand nand_52 (nand_52_out, nand_5_out, nand_5_out);
  nand nand_53 (nand_53_out, nand_6_out, nand_6_out);
  nand nand_54 (nand_54_out, nand_7_out, nand_7_out);
  nand nand_55 (nand_55_out, nand_8_out, nand_8_out);
  nand nand_56 (nand_56_out, nand_9_out, nand_9_out);
  nand nand_57 (nand_57_out, nand_10_out, nand_10_out);
  nand nand_58 (nand_58_out, nand_11_out, nand_11_out);
  nand nand_59 (nand_59_out, nand_12_out, nand_12_out);
  nand nand_60 (nand_60_out, nand_13_out, nand_13_out);
  nand nand_61 (nand_61_out, nand_14_out, nand_14_out);
  nand nand_62 (nand_62_out, nand_15_out, nand_15_out);
  nand nand_63 (nand_63_out, nand_16_out, nand_16_out);
  nand nand_64 (nand_64_out, nand_17_out, nand_17_out);
  nand nand_65 (nand_65_out, nand_18_out, nand_18_out);
  nand nand_66 (nand_66_out, nand_19_out, nand_19_out);
  nand nand_67 (nand_67_out, nand_20_out, nand_20_out);
  nand nand_68 (nand_68_out, nand_21_out, nand_22_out);
  nand nand_69 (nand_69_out, nand_23_out, nand_24_out);
  nand nand_70 (nand_70_out, nand_25_out, nand_26_out);
  nand nand_71 (nand_71_out, nand_27_out, nand_28_out);
  nand nand_72 (nand_72_out, S[2], nand_29_out);
  nand nand_73 (nand_73_out, S[2], nand_30_out);
  nand nand_74 (PCSource1, nand_31_out, nand_32_out);
  nand nand_75 (nand_75_out, S[3], nand_33_out);
  nand nand_76 (nand_76_out, S[3], nand_34_out);
  nand nand_77 (nand_77_out, nand_35_out, nand_35_out);
  nand nand_78 (nand_78_out, 1'b1, S[0]);
  nand nand_79 (nand_79_out, nand_36_out, nand_36_out);
  nand nand_80 (nand_80_out, 1'b1, S[0]);
  nand nand_81 (nand_81_out, S[3], nand_37_out);
  nand nand_82 (nand_82_out, S[3], nand_38_out);
  nand nand_83 (nand_83_out, nand_39_out, nand_40_out);
  nand nand_84 (nand_84_out, nand_41_out, S[0]);
  nand nand_85 (nand_85_out, nand_42_out, S[1]);
  nand nand_86 (nand_86_out, nand_43_out, nand_44_out);
  nand nand_87 (nand_87_out, nand_45_out, nand_46_out);
  nand nand_88 (nand_88_out, S[1], nand_47_out);
  nand nand_89 (nand_89_out, S[3], nand_48_out);
  nand nand_90 (nand_90_out, S[2], nand_49_out);
  nand nand_91 (nand_91_out, S[2], S[1]);
  nand nand_92 (nand_92_out, nand_50_out, nand_50_out);
  nand nand_93 (nand_93_out, nand_51_out, nand_51_out);
  nand nand_94 (nand_94_out, nand_52_out, nand_53_out);
  nand nand_95 (nand_95_out, nand_54_out, nand_55_out);
  nand nand_96 (nand_96_out, nand_56_out, nand_57_out);
  nand nand_97 (nand_97_out, nand_58_out, nand_59_out);
  nand nand_98 (nand_98_out, nand_60_out, nand_61_out);
  nand nand_99 (nand_99_out, nand_62_out, nand_63_out);
  nand nand_100 (nand_100_out, nand_64_out, nand_65_out);
  nand nand_101 (nand_101_out, nand_66_out, nand_67_out);
  nand nand_102 (nand_102_out, nand_68_out, nand_68_out);
  nand nand_103 (nand_103_out, nand_69_out, nand_69_out);
  nand nand_104 (nand_104_out, nand_70_out, nand_70_out);
  nand nand_105 (nand_105_out, nand_71_out, nand_71_out);
  nand nand_106 (nand_106_out, nand_72_out, nand_72_out);
  nand nand_107 (nand_107_out, 1'b1, S[0]);
  nand nand_108 (nand_108_out, nand_73_out, nand_73_out);
  nand nand_109 (nand_109_out, 1'b1, S[0]);
  nand nand_110 (PCSource0, nand_75_out, nand_76_out);
  nand nand_111 (nand_111_out, nand_77_out, nand_78_out);
  nand nand_112 (nand_112_out, nand_79_out, nand_80_out);
  nand nand_113 (ALUOp0, nand_81_out, nand_82_out);
  nand nand_114 (nand_114_out, nand_83_out, nand_83_out);
  nand nand_115 (nand_115_out, nand_84_out, nand_84_out);
  nand nand_116 (nand_116_out, nand_85_out, nand_85_out);
  nand nand_117 (nand_117_out, 1'b1, S[0]);
  nand nand_118 (nand_118_out, nand_86_out, nand_86_out);
  nand nand_119 (nand_119_out, 1'b1, S[1]);
  nand nand_120 (nand_120_out, nand_87_out, nand_87_out);
  nand nand_121 (nand_121_out, 1'b1, S[1]);
  nand nand_122 (ALUSrcA, nand_88_out, nand_89_out);
  nand nand_123 (nand_123_out, nand_90_out, nand_90_out);
  nand nand_124 (nand_124_out, 1'b1, S[0]);
  nand nand_125 (nand_125_out, nand_91_out, nand_91_out);
  nand nand_126 (nand_126_out, nand_92_out, S[0]);
  nand nand_127 (nand_127_out, nand_93_out, S[0]);
  nand nand_128 (PCWrite, nand_94_out, nand_95_out);
  nand nand_129 (PCWriteCond, nand_96_out, nand_96_out);
  nand nand_130 (IorD, nand_97_out, nand_98_out);
  nand nand_131 (MemRead, nand_99_out, nand_100_out);
  nand nand_132 (MemWrite, nand_101_out, nand_101_out);
  nand nand_133 (nand_133_out, nand_102_out, nand_103_out);
  nand nand_134 (nand_134_out, nand_104_out, nand_105_out);
  nand nand_135 (nand_135_out, nand_106_out, nand_107_out);
  nand nand_136 (nand_136_out, nand_108_out, nand_109_out);
  nand nand_137 (ALUOp1, nand_111_out, nand_112_out);
  nand nand_138 (nand_138_out, nand_114_out, nand_115_out);
  nand nand_139 (nand_139_out, nand_116_out, nand_117_out);
  nand nand_140 (nand_140_out, nand_118_out, nand_119_out);
  nand nand_141 (nand_141_out, nand_120_out, nand_121_out);
  nand nand_142 (nand_142_out, nand_123_out, nand_124_out);
  nand nand_143 (nand_143_out, nand_125_out, S[0]);
  nand nand_144 (RegDst, nand_126_out, nand_127_out);
  nand nand_145 (IRWrite, nand_133_out, nand_134_out);
  nand nand_146 (MemtoReg, nand_135_out, nand_136_out);
  nand nand_147 (ALUSrcB1, nand_138_out, nand_139_out);
  nand nand_148 (ALUSrcB0, nand_140_out, nand_141_out);
  nand nand_149 (RegWrite, nand_142_out, nand_143_out);
endmodule

module NextStage3 (
  input  [5:0] Op,
  input  [3:0] S,
  output NS3
);

  wire nand_1_out, nand_2_out, nand_3_out, nand_4_out, nand_5_out, nand_6_out, nand_7_out, nand_8_out,
       nand_9_out, nand_10_out, nand_11_out, nand_12_out, nand_13_out, nand_14_out, nand_15_out, nand_16_out,
       nand_17_out, nand_18_out, nand_19_out, nand_20_out, nand_21_out, nand_22_out, nand_23_out,
       nand_24_out, nand_25_out, nand_26_out, nand_27_out, nand_28_out, nand_29_out, nand_30_out,
       nand_31_out, nand_32_out, nand_33_out, nand_34_out, nand_35_out, nand_36_out, nand_37_out,
       nand_38_out, nand_39_out, nand_40_out, nand_41_out, nand_42_out, nand_43_out;

  nand nand_1 (nand_1_out, 1'b1, Op[5]);
  nand nand_2 (nand_2_out, 1'b1, Op[4]);
  nand nand_3 (nand_3_out, 1'b1, Op[3]);
  nand nand_4 (nand_4_out, 1'b1, Op[2]);
  nand nand_5 (nand_5_out, 1'b1, Op[1]);
  nand nand_6 (nand_6_out, 1'b1, Op[0]);
  nand nand_7 (nand_7_out, 1'b1, S[3]);
  nand nand_8 (nand_8_out, 1'b1, S[2]);
  nand nand_9 (nand_9_out, 1'b1, S[1]);
  nand nand_10 (nand_10_out, nand_1_out, nand_2_out);
  nand nand_11 (nand_11_out, nand_6_out, nand_7_out);
  nand nand_12 (nand_12_out, nand_1_out, nand_2_out);
  nand nand_13 (nand_13_out, nand_6_out, nand_7_out);
  nand nand_14 (nand_14_out, nand_10_out, nand_10_out);
  nand nand_15 (nand_15_out, nand_11_out, nand_11_out);
  nand nand_16 (nand_16_out, nand_12_out, nand_12_out);
  nand nand_17 (nand_17_out, nand_13_out, nand_13_out);
  nand nand_18 (nand_18_out, nand_14_out, nand_3_out);
  nand nand_19 (nand_19_out, nand_4_out, Op[1]);
  nand nand_20 (nand_20_out, nand_15_out, nand_8_out);
  nand nand_21 (nand_21_out, nand_9_out, S[0]);
  nand nand_22 (nand_22_out, nand_16_out, nand_3_out);
  nand nand_23 (nand_23_out, Op[2], nand_5_out);
  nand nand_24 (nand_24_out, nand_17_out, nand_8_out);
  nand nand_25 (nand_25_out, nand_9_out, S[0]);
  nand nand_26 (nand_26_out, nand_18_out, nand_18_out);
  nand nand_27 (nand_27_out, nand_19_out, nand_19_out);
  nand nand_28 (nand_28_out, nand_20_out, nand_20_out);
  nand nand_29 (nand_29_out, nand_21_out, nand_21_out);
  nand nand_30 (nand_30_out, nand_22_out, nand_22_out);
  nand nand_31 (nand_31_out, nand_23_out, nand_23_out);
  nand nand_32 (nand_32_out, nand_24_out, nand_24_out);
  nand nand_33 (nand_33_out, nand_25_out, nand_25_out);
  nand nand_34 (nand_34_out, nand_26_out, nand_27_out);
  nand nand_35 (nand_35_out, nand_28_out, nand_29_out);
  nand nand_36 (nand_36_out, nand_30_out, nand_31_out);
  nand nand_37 (nand_37_out, nand_32_out, nand_33_out);
  nand nand_38 (nand_38_out, nand_34_out, nand_34_out);
  nand nand_39 (nand_39_out, nand_35_out, nand_35_out);
  nand nand_40 (nand_40_out, nand_36_out, nand_36_out);
  nand nand_41 (nand_41_out, nand_37_out, nand_37_out);
  nand nand_42 (nand_42_out, nand_38_out, nand_39_out);
  nand nand_43 (nand_43_out, nand_40_out, nand_41_out);
  nand nand_44 (NS3, nand_42_out, nand_43_out);
endmodule

module NextStage2 (
  input  [5:0] Op,
  input  [3:0] S,
  output NS2
);

  wire nand_1_out, nand_2_out, nand_3_out, nand_4_out, nand_5_out, nand_6_out, nand_7_out, nand_8_out,
       nand_9_out, nand_10_out, nand_11_out, nand_12_out, nand_13_out, nand_14_out, nand_15_out, nand_16_out,
       nand_17_out, nand_18_out, nand_19_out, nand_20_out, nand_21_out, nand_22_out, nand_23_out,
       nand_24_out, nand_25_out, nand_26_out, nand_27_out, nand_28_out, nand_29_out, nand_30_out,
       nand_31_out, nand_32_out, nand_33_out, nand_34_out, nand_35_out, nand_36_out, nand_37_out,
       nand_38_out, nand_39_out, nand_40_out, nand_41_out, nand_42_out, nand_43_out, nand_44_out,
       nand_45_out, nand_46_out, nand_47_out, nand_48_out, nand_49_out, nand_50_out, nand_51_out,
       nand_52_out, nand_53_out;

  nand nand_1 (nand_1_out, 1'b1, Op[5]);
  nand nand_2 (nand_2_out, 1'b1, Op[4]);
  nand nand_3 (nand_3_out, 1'b1, Op[3]);
  nand nand_4 (nand_4_out, 1'b1, Op[2]);
  nand nand_5 (nand_5_out, 1'b1, Op[1]);
  nand nand_6 (nand_6_out, 1'b1, Op[0]);
  nand nand_7 (nand_7_out, 1'b1, S[3]);
  nand nand_8 (nand_8_out, 1'b1, S[2]);
  nand nand_9 (nand_9_out, 1'b1, S[0]);
  nand nand_10 (nand_10_out, nand_1_out, nand_2_out);
  nand nand_11 (nand_11_out, Op[5], nand_2_out);
  nand nand_12 (nand_12_out, nand_10_out, nand_10_out);
  nand nand_13 (nand_13_out, nand_11_out, nand_11_out);
  nand nand_14 (nand_14_out, nand_12_out, nand_3_out);
  nand nand_15 (nand_15_out, nand_4_out, nand_5_out);
  nand nand_16 (nand_16_out, nand_6_out, nand_7_out);
  nand nand_17 (nand_17_out, nand_8_out, S[0]);
  nand nand_18 (nand_18_out, nand_13_out, Op[3]);
  nand nand_19 (nand_19_out, nand_4_out, Op[1]);
  nand nand_20 (nand_20_out, Op[0], nand_7_out);
  nand nand_21 (nand_21_out, nand_8_out, S[1]);
  nand nand_22 (nand_22_out, nand_14_out, nand_14_out);
  nand nand_23 (nand_23_out, nand_15_out, nand_15_out);
  nand nand_24 (nand_24_out, nand_16_out, nand_16_out);
  nand nand_25 (nand_25_out, nand_17_out, nand_17_out);
  nand nand_26 (nand_26_out, nand_18_out, nand_18_out);
  nand nand_27 (nand_27_out, nand_19_out, nand_19_out);
  nand nand_28 (nand_28_out, nand_20_out, nand_20_out);
  nand nand_29 (nand_29_out, nand_21_out, nand_21_out);
  nand nand_30 (nand_30_out, nand_22_out, nand_23_out);
  nand nand_31 (nand_31_out, nand_24_out, nand_25_out);
  nand nand_32 (nand_32_out, nand_7_out, nand_8_out);
  nand nand_33 (nand_33_out, S[1], S[0]);
  nand nand_34 (nand_34_out, nand_7_out, S[2]);
  nand nand_35 (nand_35_out, S[1], nand_9_out);
  nand nand_36 (nand_36_out, nand_26_out, nand_27_out);
  nand nand_37 (nand_37_out, nand_28_out, nand_29_out);
  nand nand_38 (nand_38_out, nand_30_out, nand_30_out);
  nand nand_39 (nand_39_out, nand_31_out, nand_31_out);
  nand nand_40 (nand_40_out, nand_32_out, nand_32_out);
  nand nand_41 (nand_41_out, nand_33_out, nand_33_out);
  nand nand_42 (nand_42_out, nand_34_out, nand_34_out);
  nand nand_43 (nand_43_out, nand_35_out, nand_35_out);
  nand nand_44 (nand_44_out, nand_36_out, nand_36_out);
  nand nand_45 (nand_45_out, nand_37_out, nand_37_out);
  nand nand_46 (nand_46_out, nand_38_out, nand_39_out);
  nand nand_47 (nand_47_out, nand_40_out, nand_41_out);
  nand nand_48 (nand_48_out, nand_42_out, nand_43_out);
  nand nand_49 (nand_49_out, nand_44_out, nand_45_out);
  nand nand_50 (nand_50_out, nand_46_out, nand_47_out);
  nand nand_51 (nand_51_out, nand_48_out, nand_49_out);
  nand nand_52 (nand_52_out, nand_50_out, nand_50_out);
  nand nand_53 (nand_53_out, nand_51_out, nand_51_out);
  nand nand_54 (NS2, nand_52_out, nand_53_out);
endmodule

module NestStage1 (
  input  [5:0] Op,
  input  [3:0] S,
  output NS1
);

  wire nand_1_out, nand_2_out, nand_3_out, nand_4_out, nand_5_out, nand_6_out, nand_7_out, nand_8_out,
       nand_9_out, nand_10_out, nand_11_out, nand_12_out, nand_13_out, nand_14_out, nand_15_out, nand_16_out,
       nand_17_out, nand_18_out, nand_19_out, nand_20_out, nand_21_out, nand_22_out, nand_23_out,
       nand_24_out, nand_25_out, nand_26_out, nand_27_out, nand_28_out, nand_29_out, nand_30_out,
       nand_31_out, nand_32_out, nand_33_out, nand_34_out, nand_35_out, nand_36_out, nand_37_out,
       nand_38_out, nand_39_out, nand_40_out, nand_41_out, nand_42_out, nand_43_out, nand_44_out,
       nand_45_out, nand_46_out, nand_47_out, nand_48_out, nand_49_out, nand_50_out, nand_51_out,
       nand_52_out, nand_53_out, nand_54_out, nand_55_out, nand_56_out, nand_57_out, nand_58_out,
       nand_59_out, nand_60_out, nand_61_out, nand_62_out, nand_63_out, nand_64_out, nand_65_out,
       nand_66_out, nand_67_out, nand_68_out, nand_69_out, nand_70_out, nand_71_out, nand_72_out,
       nand_73_out, nand_74_out, nand_75_out, nand_76_out, nand_77_out, nand_78_out, nand_79_out,
       nand_80_out, nand_81_out, nand_82_out, nand_83_out, nand_84_out, nand_85_out, nand_86_out,
       nand_87_out, nand_88_out, nand_89_out, nand_90_out, nand_91_out, nand_92_out, nand_93_out,
       nand_94_out, nand_95_out, nand_96_out, nand_97_out, nand_98_out, nand_99_out, nand_100_out,
       nand_101_out, nand_102_out, nand_103_out, nand_104_out, nand_105_out, nand_106_out, nand_107_out,
       nand_108_out, nand_109_out, nand_110_out, nand_111_out, nand_112_out, nand_113_out;

  nand nand_1 (nand_1_out, 1'b1, Op[5]);
  nand nand_2 (nand_2_out, 1'b1, Op[4]);
  nand nand_3 (nand_3_out, 1'b1, Op[3]);
  nand nand_4 (nand_4_out, 1'b1, Op[2]);
  nand nand_5 (nand_5_out, 1'b1, Op[1]);
  nand nand_6 (nand_6_out, 1'b1, Op[0]);
  nand nand_7 (nand_7_out, 1'b1, S[3]);
  nand nand_8 (nand_8_out, 1'b1, S[2]);
  nand nand_9 (nand_9_out, 1'b1, S[1]);
  nand nand_10 (nand_10_out, 1'b1, S[0]);
  nand nand_11 (nand_11_out, nand_1_out, nand_2_out);
  nand nand_12 (nand_12_out, nand_6_out, nand_7_out);
  nand nand_13 (nand_13_out, nand_11_out, nand_11_out);
  nand nand_14 (nand_14_out, nand_12_out, nand_12_out);
  nand nand_15 (nand_15_out, nand_13_out, nand_3_out);
  nand nand_16 (nand_16_out, nand_4_out, nand_5_out);
  nand nand_17 (nand_17_out, nand_14_out, nand_8_out);
  nand nand_18 (nand_18_out, nand_9_out, S[0]);
  nand nand_19 (nand_19_out, nand_2_out, nand_7_out);
  nand nand_20 (nand_20_out, Op[5], nand_2_out);
  nand nand_21 (nand_21_out, Op[5], nand_2_out);
  nand nand_22 (nand_22_out, nand_15_out, nand_15_out);
  nand nand_23 (nand_23_out, nand_16_out, nand_16_out);
  nand nand_24 (nand_24_out, nand_17_out, nand_17_out);
  nand nand_25 (nand_25_out, nand_18_out, nand_18_out);
  nand nand_26 (nand_26_out, nand_19_out, nand_19_out);
  nand nand_27 (nand_27_out, nand_20_out, nand_20_out);
  nand nand_28 (nand_28_out, nand_21_out, nand_21_out);
  nand nand_29 (nand_29_out, nand_22_out, nand_23_out);
  nand nand_30 (nand_30_out, nand_24_out, nand_25_out);
  nand nand_31 (nand_31_out, nand_26_out, S[2]);
  nand nand_32 (nand_32_out, S[1], nand_10_out);
  nand nand_33 (nand_33_out, nand_3_out, nand_7_out);
  nand nand_34 (nand_34_out, nand_4_out, nand_7_out);
  nand nand_35 (nand_35_out, nand_6_out, nand_7_out);
  nand nand_36 (nand_36_out, Op[1], nand_7_out);
  nand nand_37 (nand_37_out, Op[5], nand_7_out);
  nand nand_38 (nand_38_out, nand_27_out, nand_4_out);
  nand nand_39 (nand_39_out, Op[1], Op[0]);
  nand nand_40 (nand_40_out, nand_7_out, nand_8_out);
  nand nand_41 (nand_41_out, nand_9_out, S[0]);
  nand nand_42 (nand_42_out, nand_28_out, nand_3_out);
  nand nand_43 (nand_43_out, nand_4_out, Op[1]);
  nand nand_44 (nand_44_out, Op[0], nand_7_out);
  nand nand_45 (nand_45_out, S[1], nand_10_out);
  nand nand_46 (nand_46_out, nand_29_out, nand_29_out);
  nand nand_47 (nand_47_out, nand_30_out, nand_30_out);
  nand nand_48 (nand_48_out, nand_31_out, nand_31_out);
  nand nand_49 (nand_49_out, nand_32_out, nand_32_out);
  nand nand_50 (nand_50_out, nand_33_out, nand_33_out);
  nand nand_51 (nand_51_out, nand_34_out, nand_34_out);
  nand nand_52 (nand_52_out, nand_35_out, nand_35_out);
  nand nand_53 (nand_53_out, nand_36_out, nand_36_out);
  nand nand_54 (nand_54_out, nand_37_out, nand_37_out);
  nand nand_55 (nand_55_out, nand_38_out, nand_38_out);
  nand nand_56 (nand_56_out, nand_39_out, nand_39_out);
  nand nand_57 (nand_57_out, nand_40_out, nand_40_out);
  nand nand_58 (nand_58_out, nand_41_out, nand_41_out);
  nand nand_59 (nand_59_out, nand_42_out, nand_42_out);
  nand nand_60 (nand_60_out, nand_43_out, nand_43_out);
  nand nand_61 (nand_61_out, nand_44_out, nand_44_out);
  nand nand_62 (nand_62_out, nand_45_out, nand_45_out);
  nand nand_63 (nand_63_out, nand_46_out, nand_47_out);
  nand nand_64 (nand_64_out, nand_48_out, nand_49_out);
  nand nand_65 (nand_65_out, nand_50_out, S[2]);
  nand nand_66 (nand_66_out, S[1], nand_10_out);
  nand nand_67 (nand_67_out, nand_51_out, S[2]);
  nand nand_68 (nand_68_out, S[1], nand_10_out);
  nand nand_69 (nand_69_out, nand_52_out, S[2]);
  nand nand_70 (nand_70_out, S[1], nand_10_out);
  nand nand_71 (nand_71_out, nand_53_out, S[2]);
  nand nand_72 (nand_72_out, S[1], nand_10_out);
  nand nand_73 (nand_73_out, nand_54_out, S[2]);
  nand nand_74 (nand_74_out, S[1], nand_10_out);
  nand nand_75 (nand_75_out, nand_55_out, nand_56_out);
  nand nand_76 (nand_76_out, nand_57_out, nand_58_out);
  nand nand_77 (nand_77_out, nand_59_out, nand_60_out);
  nand nand_78 (nand_78_out, nand_61_out, nand_62_out);
  nand nand_79 (nand_79_out, nand_63_out, nand_64_out);
  nand nand_80 (nand_80_out, nand_65_out, nand_65_out);
  nand nand_81 (nand_81_out, nand_66_out, nand_66_out);
  nand nand_82 (nand_82_out, nand_67_out, nand_67_out);
  nand nand_83 (nand_83_out, nand_68_out, nand_68_out);
  nand nand_84 (nand_84_out, nand_69_out, nand_69_out);
  nand nand_85 (nand_85_out, nand_70_out, nand_70_out);
  nand nand_86 (nand_86_out, nand_71_out, nand_71_out);
  nand nand_87 (nand_87_out, nand_72_out, nand_72_out);
  nand nand_88 (nand_88_out, nand_73_out, nand_73_out);
  nand nand_89 (nand_89_out, nand_74_out, nand_74_out);
  nand nand_90 (nand_90_out, nand_75_out, nand_75_out);
  nand nand_91 (nand_91_out, nand_76_out, nand_76_out);
  nand nand_92 (nand_92_out, nand_77_out, nand_77_out);
  nand nand_93 (nand_93_out, nand_78_out, nand_78_out);
  nand nand_94 (nand_94_out, nand_79_out, nand_79_out);
  nand nand_95 (nand_95_out, nand_80_out, nand_81_out);
  nand nand_96 (nand_96_out, nand_82_out, nand_83_out);
  nand nand_97 (nand_97_out, nand_84_out, nand_85_out);
  nand nand_98 (nand_98_out, nand_86_out, nand_87_out);
  nand nand_99 (nand_99_out, nand_88_out, nand_89_out);
  nand nand_100 (nand_100_out, nand_90_out, nand_91_out);
  nand nand_101 (nand_101_out, nand_92_out, nand_93_out);
  nand nand_102 (nand_102_out, nand_94_out, nand_95_out);
  nand nand_103 (nand_103_out, nand_96_out, nand_97_out);
  nand nand_104 (nand_104_out, nand_98_out, nand_99_out);
  nand nand_105 (nand_105_out, nand_100_out, nand_101_out);
  nand nand_106 (nand_106_out, nand_102_out, nand_102_out);
  nand nand_107 (nand_107_out, nand_103_out, nand_103_out);
  nand nand_108 (nand_108_out, nand_104_out, nand_104_out);
  nand nand_109 (nand_109_out, nand_105_out, nand_105_out);
  nand nand_110 (nand_110_out, nand_106_out, nand_107_out);
  nand nand_111 (nand_111_out, nand_108_out, nand_109_out);
  nand nand_112 (nand_112_out, nand_110_out, nand_110_out);
  nand nand_113 (nand_113_out, nand_111_out, nand_111_out);
  nand nand_114 (NS1, nand_112_out, nand_113_out);
endmodule

module NextStage0 (
  input  [5:0] Op,
  input  [3:0] S,
  output NS0
);

  wire nand_1_out, nand_2_out, nand_3_out, nand_4_out, nand_5_out, nand_6_out, nand_7_out, nand_8_out,
       nand_9_out, nand_10_out, nand_11_out, nand_12_out, nand_13_out, nand_14_out, nand_15_out, nand_16_out,
       nand_17_out, nand_18_out, nand_19_out, nand_20_out, nand_21_out, nand_22_out, nand_23_out,
       nand_24_out, nand_25_out, nand_26_out, nand_27_out, nand_28_out, nand_29_out, nand_30_out,
       nand_31_out, nand_32_out, nand_33_out, nand_34_out, nand_35_out, nand_36_out, nand_37_out,
       nand_38_out, nand_39_out, nand_40_out, nand_41_out, nand_42_out, nand_43_out, nand_44_out,
       nand_45_out, nand_46_out, nand_47_out, nand_48_out, nand_49_out, nand_50_out, nand_51_out,
       nand_52_out, nand_53_out, nand_54_out, nand_55_out, nand_56_out, nand_57_out, nand_58_out,
       nand_59_out, nand_60_out, nand_61_out, nand_62_out, nand_63_out, nand_64_out, nand_65_out,
       nand_66_out, nand_67_out, nand_68_out, nand_69_out;

  nand nand_1 (nand_1_out, 1'b1, Op[5]);
  nand nand_2 (nand_2_out, 1'b1, Op[4]);
  nand nand_3 (nand_3_out, 1'b1, Op[3]);
  nand nand_4 (nand_4_out, 1'b1, Op[2]);
  nand nand_5 (nand_5_out, 1'b1, Op[1]);
  nand nand_6 (nand_6_out, 1'b1, Op[0]);
  nand nand_7 (nand_7_out, 1'b1, S[3]);
  nand nand_8 (nand_8_out, 1'b1, S[2]);
  nand nand_9 (nand_9_out, 1'b1, S[1]);
  nand nand_10 (nand_10_out, 1'b1, S[0]);
  nand nand_11 (nand_11_out, nand_1_out, nand_2_out);
  nand nand_12 (nand_12_out, nand_1_out, nand_2_out);
  nand nand_13 (nand_13_out, nand_11_out, nand_11_out);
  nand nand_14 (nand_14_out, nand_12_out, nand_12_out);
  nand nand_15 (nand_15_out, nand_7_out, nand_8_out);
  nand nand_16 (nand_16_out, nand_9_out, nand_10_out);
  nand nand_17 (nand_17_out, nand_7_out, S[2]);
  nand nand_18 (nand_18_out, S[1], nand_10_out);
  nand nand_19 (nand_19_out, nand_13_out, nand_3_out);
  nand nand_20 (nand_20_out, nand_4_out, nand_5_out);
  nand nand_21 (nand_21_out, Op[0], nand_7_out);
  nand nand_22 (nand_22_out, nand_8_out, nand_9_out);
  nand nand_23 (nand_23_out, nand_14_out, nand_3_out);
  nand nand_24 (nand_24_out, nand_4_out, Op[1]);
  nand nand_25 (nand_25_out, nand_6_out, nand_7_out);
  nand nand_26 (nand_26_out, nand_8_out, nand_9_out);
  nand nand_27 (nand_27_out, Op[5], nand_2_out);
  nand nand_28 (nand_28_out, nand_4_out, Op[1]);
  nand nand_29 (nand_29_out, Op[0], nand_7_out);
  nand nand_30 (nand_30_out, nand_8_out, nand_10_out);
  nand nand_31 (nand_31_out, nand_15_out, nand_15_out);
  nand nand_32 (nand_32_out, nand_16_out, nand_16_out);
  nand nand_33 (nand_33_out, nand_17_out, nand_17_out);
  nand nand_34 (nand_34_out, nand_18_out, nand_18_out);
  nand nand_35 (nand_35_out, nand_19_out, nand_19_out);
  nand nand_36 (nand_36_out, nand_20_out, nand_20_out);
  nand nand_37 (nand_37_out, nand_21_out, nand_21_out);
  nand nand_38 (nand_38_out, nand_22_out, nand_22_out);
  nand nand_39 (nand_39_out, nand_23_out, nand_23_out);
  nand nand_40 (nand_40_out, nand_24_out, nand_24_out);
  nand nand_41 (nand_41_out, nand_25_out, nand_25_out);
  nand nand_42 (nand_42_out, nand_26_out, nand_26_out);
  nand nand_43 (nand_43_out, nand_27_out, nand_27_out);
  nand nand_44 (nand_44_out, nand_28_out, nand_28_out);
  nand nand_45 (nand_45_out, nand_29_out, nand_29_out);
  nand nand_46 (nand_46_out, nand_30_out, nand_30_out);
  nand nand_47 (nand_47_out, nand_31_out, nand_32_out);
  nand nand_48 (nand_48_out, nand_33_out, nand_34_out);
  nand nand_49 (nand_49_out, nand_35_out, nand_36_out);
  nand nand_50 (nand_50_out, nand_37_out, nand_38_out);
  nand nand_51 (nand_51_out, nand_39_out, nand_40_out);
  nand nand_52 (nand_52_out, nand_41_out, nand_42_out);
  nand nand_53 (nand_53_out, nand_43_out, nand_44_out);
  nand nand_54 (nand_54_out, nand_45_out, nand_46_out);
  nand nand_55 (nand_55_out, nand_47_out, nand_48_out);
  nand nand_56 (nand_56_out, nand_49_out, nand_49_out);
  nand nand_57 (nand_57_out, nand_50_out, nand_50_out);
  nand nand_58 (nand_58_out, nand_51_out, nand_51_out);
  nand nand_59 (nand_59_out, nand_52_out, nand_52_out);
  nand nand_60 (nand_60_out, nand_53_out, nand_53_out);
  nand nand_61 (nand_61_out, nand_54_out, nand_54_out);
  nand nand_62 (nand_62_out, nand_55_out, nand_55_out);
  nand nand_63 (nand_63_out, nand_56_out, nand_57_out);
  nand nand_64 (nand_64_out, nand_58_out, nand_59_out);
  nand nand_65 (nand_65_out, nand_60_out, nand_61_out);
  nand nand_66 (nand_66_out, nand_62_out, nand_63_out);
  nand nand_67 (nand_67_out, nand_64_out, nand_65_out);
  nand nand_68 (nand_68_out, nand_66_out, nand_66_out);
  nand nand_69 (nand_69_out, nand_67_out, nand_67_out);
  nand nand_70 (NS0, nand_68_out, nand_69_out);
endmodule

module NextStage (
  input  [5:0] in_1,
  input  [3:0] in_2,
  output [3:0] out_3
);

  NextStage3 nextstage3_1 (.Op(in_1), .S(in_2), .NS3(out_3[3]));
  NextStage2 nextstage2_1 (.Op(in_1), .S(in_2), .NS2(out_3[2]));
  NestStage1 neststage1_1 (.Op(in_1), .S(in_2), .NS1(out_3[1]));
  NextStage0 nextstage0_1 (.Op(in_1), .S(in_2), .NS0(out_3[0]));
endmodule

module Control_unit (
  input  [5:0] Opcode,
  input  Clock,
  input  Reset,
  output PCWrite,
  output PCWriteCond,
  output IorD,
  output MemRead,
  output MemWrite,
  output IRWrite,
  output MemroReg,
  output PCSource1,
  output PCSource0,
  output ALUOp1,
  output ALUOp0,
  output ALUSrcB1,
  output ALUSrcB0,
  output ALUSrcA,
  output RegWrite,
  output RegDst,
  output [3:0] CurrentState
);

  wire [3:0] nextstage_1_out_3;

  NextStage nextstage_1 (.in_1(Opcode), .in_2(CurrentState), .out_3(nextstage_1_out_3));
  Register #(.width(4)) register_1 (.D(nextstage_1_out_3), .clk(Clock), .Q(CurrentState), .clr(Reset));  // open: en
  Datapath_outputs datapath_outputs_1 (
    .S(CurrentState), .PCWrite(PCWrite), .PCWriteCond(PCWriteCond), .IorD(IorD), .MemRead(MemRead),
    .MemWrite(MemWrite), .IRWrite(IRWrite), .MemtoReg(MemroReg), .PCSource1(PCSource1),
    .PCSource0(PCSource0), .ALUOp1(ALUOp1), .ALUOp0(ALUOp0), .ALUSrcB1(ALUSrcB1), .ALUSrcB0(ALUSrcB0),
    .ALUSrcA(ALUSrcA), .RegWrite(RegWrite), .RegDst(RegDst));
endmodule

module ALU_Control (
  input  ALUOp0,
  input  ALUOp1,
  input  F3,
  input  F2,
  input  F1,
  input  F0,
  output Op3,
  output Op2,
  output Op1,
  output Op0
);

  wire and_2_out, not_1_out, not_2_out, not_3_out, or_1_out;

  or or_1 (or_1_out, F3, F0);
  and and_1 (Op0, ALUOp1, or_1_out);
  and and_2 (and_2_out, ALUOp1, F1);
  not not_1 (not_1_out, F2);
  not not_2 (not_2_out, ALUOp1);
  not not_3 (not_3_out, ALUOp0);
  or or_2 (Op1, not_1_out, not_2_out);
  and and_3 (Op3, ALUOp0, not_3_out);
  or or_3 (Op2, ALUOp0, and_2_out);
endmodule

module InstructionReg (
  input  [31:0] in_1,
  input  WE,
  input  Clock,
  input  Reset,
  output [15:0] out_5,
  output [4:0] rt,
  output [4:0] rs,
  output [5:0] Opcode
);

  Register #(.width(32)) register_1 (.D(in_1), .en(WE), .clk(Clock), .Q({Opcode, rs, rt, out_5}), .clr(Reset));
endmodule

module ALU (
  input  [3:0] Op,
  input  [31:0] A,
  input  [31:0] B,
  input  [4:0] Shamt,
  output [31:0] Res,
  output Zero
);

  wire comparator_1_lt;
  wire [31:0] Add, E, LessThan, N_or, Ou, ShiftLeft, ShiftRight, Sub, Xou;

  Adder #(.width(32)) adder_1 (.a(A), .b(B), .out(Add));  // open: cin, cout
  Subtractor #(.width(32)) subtractor_1 (.a(A), .b(B), .out(Sub));  // open: bin, bout
  assign E = A & B;  // AND_Gate and_1, 32 bits wide
  assign Ou = A | B;  // OR_Gate or_1, 32 bits wide
  assign Xou = A ^ B;  // XOR_Gate xor_1, 32 bits wide
  Comparator #(.width(32)) comparator_1 (.a(A), .b(B), .lt(comparator_1_lt));  // open: gt, eq
  Shifter #(.width(32)) shifter_1 (.in(B), .\dist (Shamt), .out(ShiftLeft));
  Shifter #(.shift("lr"), .width(32)) shifter_2 (.in(B), .\dist (Shamt), .out(ShiftRight));
  assign N_or = ~(A | B);  // NOR_Gate nor_1, 32 bits wide
  assign LessThan = {{31{comparator_1_lt}}, comparator_1_lt};  // Bit_Extender bit_extender_1
  Multiplexer #(.select(4), .width(32)) multiplexer_1 (
    .in0(E), .in1(Ou), .in2(Add), .in6(Sub), .in7(LessThan), .out(Res), .sel(Op));  // open: in3, in4, in5, in8, in9, in10, in11, in12, in13, in14, in15
  Comparator #(.width(32)) comparator_2 (.a(Res), .b({32{1'b0}}), .eq(Zero));  // open: gt, lt

  // Other names for the same wires on the sheet: ASign = A[31]; ALUCtl[3:0] = Op; ALUCtl0 = Op[0]; ALUCtl1 = Op[1];
  //   ALUCtl2 = Op[2]; BSign = B[31]
endmodule

module RegFile (
  input  [4:0] rs,
  input  [4:0] rt,
  input  [4:0] WrAddr,
  input  [31:0] WriteData,
  input  WrReg,
  input  in_6,
  input  Reset,
  output [31:0] RdData1,
  output [31:0] RdData2
);

  wire WrReg0, WrReg1, WrReg2, WrReg3, WrReg4, WrReg5, WrReg6, WrReg7, WrReg8, WrReg9, WrReg10, WrReg11,
       WrReg12, WrReg13, WrReg14, WrReg15, WrReg16, WrReg17, WrReg18, WrReg19, WrReg20, WrReg21, WrReg22,
       WrReg23, WrReg24, WrReg25, WrReg26, WrReg27, WrReg28, WrReg29, WrReg30, WrReg31;
  wire [31:0] RegData1, RegData2, RegData3, RegData4, RegData5, RegData6, RegData7, RegData8, RegData9,
       RegData10, RegData11, RegData12, RegData13, RegData14, RegData15, RegData16, RegData17, RegData18,
       RegData19, RegData20, RegData21, RegData22, RegData23, RegData24, RegData25, RegData26, RegData27,
       RegData28, RegData29, RegData30, RegData31;

  Demultiplexer #(.select(5)) demultiplexer_1 (
    .out0(WrReg0), .out1(WrReg1), .out2(WrReg2), .out3(WrReg3), .out4(WrReg4), .out5(WrReg5), .out6(WrReg6),
    .out7(WrReg7), .out8(WrReg8), .out9(WrReg9), .out10(WrReg10), .out11(WrReg11), .out12(WrReg12),
    .out13(WrReg13), .out14(WrReg14), .out15(WrReg15), .out16(WrReg16), .out17(WrReg17), .out18(WrReg18),
    .out19(WrReg19), .out20(WrReg20), .out21(WrReg21), .out22(WrReg22), .out23(WrReg23), .out24(WrReg24),
    .out25(WrReg25), .out26(WrReg26), .out27(WrReg27), .out28(WrReg28), .out29(WrReg29), .out30(WrReg30),
    .out31(WrReg31), .in(WrReg), .sel(WrAddr));
  Register #(.width(32)) Reg1 (.D(WriteData), .en(WrReg1), .clk(in_6), .Q(RegData1), .clr(Reset));
  Register #(.width(32)) Reg2 (.D(WriteData), .en(WrReg2), .clk(in_6), .Q(RegData2), .clr(Reset));
  Register #(.width(32)) Reg3 (.D(WriteData), .en(WrReg3), .clk(in_6), .Q(RegData3), .clr(Reset));
  Register #(.width(32)) Reg4 (.D(WriteData), .en(WrReg4), .clk(in_6), .Q(RegData4), .clr(Reset));
  Register #(.width(32)) Reg5 (.D(WriteData), .en(WrReg5), .clk(in_6), .Q(RegData5), .clr(Reset));
  Register #(.width(32)) Reg6 (.D(WriteData), .en(WrReg6), .clk(in_6), .Q(RegData6), .clr(Reset));
  Register #(.width(32)) Reg7 (.D(WriteData), .en(WrReg7), .clk(in_6), .Q(RegData7), .clr(Reset));
  Register #(.width(32)) Reg8 (.D(WriteData), .en(WrReg8), .clk(in_6), .Q(RegData8), .clr(Reset));
  Register #(.width(32)) Reg9 (.D(WriteData), .en(WrReg9), .clk(in_6), .Q(RegData9), .clr(Reset));
  Register #(.width(32)) Reg10 (.D(WriteData), .en(WrReg10), .clk(in_6), .Q(RegData10), .clr(Reset));
  Register #(.width(32)) Reg11 (.D(WriteData), .en(WrReg11), .clk(in_6), .Q(RegData11), .clr(Reset));
  Register #(.width(32)) Reg12 (.D(WriteData), .en(WrReg12), .clk(in_6), .Q(RegData12), .clr(Reset));
  Register #(.width(32)) Reg13 (.D(WriteData), .en(WrReg13), .clk(in_6), .Q(RegData13), .clr(Reset));
  Register #(.width(32)) Reg14 (.D(WriteData), .en(WrReg14), .clk(in_6), .Q(RegData14), .clr(Reset));
  Register #(.width(32)) Reg15 (.D(WriteData), .en(WrReg15), .clk(in_6), .Q(RegData15), .clr(Reset));
  Register #(.width(32)) Reg16 (.D(WriteData), .en(WrReg16), .clk(in_6), .Q(RegData16), .clr(Reset));
  Register #(.width(32)) Reg17 (.D(WriteData), .en(WrReg17), .clk(in_6), .Q(RegData17), .clr(Reset));
  Register #(.width(32)) Reg18 (.D(WriteData), .en(WrReg18), .clk(in_6), .Q(RegData18), .clr(Reset));
  Register #(.width(32)) Reg19 (.D(WriteData), .en(WrReg19), .clk(in_6), .Q(RegData19), .clr(Reset));
  Register #(.width(32)) Reg20 (.D(WriteData), .en(WrReg20), .clk(in_6), .Q(RegData20), .clr(Reset));
  Register #(.width(32)) Reg21 (.D(WriteData), .en(WrReg21), .clk(in_6), .Q(RegData21), .clr(Reset));
  Register #(.width(32)) Reg22 (.D(WriteData), .en(WrReg22), .clk(in_6), .Q(RegData22), .clr(Reset));
  Register #(.width(32)) Reg23 (.D(WriteData), .en(WrReg23), .clk(in_6), .Q(RegData23));  // open: clr
  Register #(.width(32)) Reg24 (.D(WriteData), .en(WrReg24), .clk(in_6), .Q(RegData24), .clr(Reset));
  Register #(.width(32)) Reg25 (.D(WriteData), .en(WrReg25), .clk(in_6), .Q(RegData25), .clr(Reset));
  Register #(.width(32)) Reg26 (.D(WriteData), .en(WrReg26), .clk(in_6), .Q(RegData26), .clr(Reset));
  Register #(.width(32)) Reg27 (.D(WriteData), .en(WrReg27), .clk(in_6), .Q(RegData27), .clr(Reset));
  Register #(.width(32)) Reg28 (.D(WriteData), .en(WrReg28), .clk(in_6), .Q(RegData28), .clr(Reset));
  Register #(.width(32)) Reg29 (.D(WriteData), .en(WrReg29), .clk(in_6), .Q(RegData29), .clr(Reset));
  Register #(.width(32)) Reg30 (.D(WriteData), .en(WrReg30), .clk(in_6), .Q(RegData30), .clr(Reset));
  Register #(.width(32)) Reg31 (.D(WriteData), .en(WrReg31), .clk(in_6), .Q(RegData31), .clr(Reset));
  Multiplexer #(.select(5), .width(32)) multiplexer_1 (
    .in0({32{1'b0}}), .in1(RegData1), .in2(RegData2), .in3(RegData3), .in4(RegData4), .in5(RegData5),
    .in6(RegData6), .in7(RegData7), .in8(RegData8), .in9(RegData9), .in10(RegData10), .in11(RegData11),
    .in12(RegData12), .in13(RegData13), .in14(RegData14), .in15(RegData15), .in16(RegData16),
    .in17(RegData17), .in18(RegData18), .in19(RegData19), .in20(RegData20), .in21(RegData21),
    .in22(RegData22), .in23(RegData23), .in24(RegData24), .in25(RegData25), .in26(RegData26),
    .in27(RegData27), .in28(RegData28), .in29(RegData29), .in30(RegData30), .in31(RegData31), .out(RdData1),
    .sel(rs));
  Multiplexer #(.select(5), .width(32)) multiplexer_2 (
    .in0({32{1'b0}}), .in1(RegData1), .in2(RegData2), .in3(RegData3), .in4(RegData4), .in5(RegData5),
    .in6(RegData6), .in7(RegData7), .in8(RegData8), .in9(RegData9), .in10(RegData10), .in11(RegData11),
    .in12(RegData12), .in13(RegData13), .in14(RegData14), .in15(RegData15), .in16(RegData16),
    .in17(RegData17), .in18(RegData18), .in19(RegData19), .in20(RegData20), .in21(RegData21),
    .in22(RegData22), .in23(RegData23), .in24(RegData24), .in25(RegData25), .in26(RegData26),
    .in27(RegData27), .in28(RegData28), .in29(RegData29), .in30(RegData30), .in31(RegData31), .out(RdData2),
    .sel(rt));

  // Other names for the same wires on the sheet: clk = in_6; WrData[31:0] = WriteData
endmodule

module OperationsALU (
  input  Op3,
  input  Op2,
  input  Op1,
  input  Op0,
  output add,
  output sub,
  output e,
  output ou
);

  wire nand_1_out, nand_2_out, nand_3_out, nand_4_out, nand_5_out, nand_6_out, nand_7_out, nand_8_out,
       nand_9_out, nand_10_out, nand_11_out, nand_12_out, nand_13_out, nand_14_out, nand_15_out, nand_16_out,
       nand_17_out, nand_18_out, nand_19_out, nand_20_out, nand_21_out, nand_22_out, nand_23_out, nand_24_out;

  nand nand_1 (nand_1_out, 1'b1, Op3);
  nand nand_2 (nand_2_out, 1'b1, Op2);
  nand nand_3 (nand_3_out, 1'b1, Op1);
  nand nand_4 (nand_4_out, 1'b1, Op0);
  nand nand_5 (nand_5_out, nand_1_out, nand_2_out);
  nand nand_6 (nand_6_out, Op1, nand_4_out);
  nand nand_7 (nand_7_out, nand_1_out, Op2);
  nand nand_8 (nand_8_out, Op1, nand_4_out);
  nand nand_9 (nand_9_out, nand_1_out, nand_2_out);
  nand nand_10 (nand_10_out, nand_3_out, nand_4_out);
  nand nand_11 (nand_11_out, nand_1_out, nand_2_out);
  nand nand_12 (nand_12_out, nand_3_out, Op0);
  nand nand_13 (nand_13_out, nand_5_out, nand_5_out);
  nand nand_14 (nand_14_out, nand_6_out, nand_6_out);
  nand nand_15 (nand_15_out, nand_7_out, nand_7_out);
  nand nand_16 (nand_16_out, nand_8_out, nand_8_out);
  nand nand_17 (nand_17_out, nand_9_out, nand_9_out);
  nand nand_18 (nand_18_out, nand_10_out, nand_10_out);
  nand nand_19 (nand_19_out, nand_11_out, nand_11_out);
  nand nand_20 (nand_20_out, nand_12_out, nand_12_out);
  nand nand_21 (nand_21_out, nand_13_out, nand_14_out);
  nand nand_22 (nand_22_out, nand_15_out, nand_16_out);
  nand nand_23 (nand_23_out, nand_17_out, nand_18_out);
  nand nand_24 (nand_24_out, nand_19_out, nand_20_out);
  nand nand_25 (add, nand_21_out, nand_21_out);
  nand nand_26 (sub, nand_22_out, nand_22_out);
  nand nand_27 (e, nand_23_out, nand_23_out);
  nand nand_28 (ou, nand_24_out, nand_24_out);
endmodule
